# Fritzing sketch uv_lantern (saved by Fritzing 0.9.3b)
perfboards: 1

parts:
  LED3 = LEDs [package=led10mm]
  LED4 = LEDs [package=led10mm]
  LED5 = LEDs [package=led10mm]
  LED6 = LEDs [package=led10mm]
  LED7 = LEDs [package=led10mm]
  LED10 = LEDs [package=led10mm]
  LED11 = LEDs [package=led10mm]
  LED14 = LEDs [package=led10mm]
  LED15 = LEDs [package=led10mm]
  LED16 = LEDs [package=led10mm]
  LED18 = LEDs [package=led10mm]
  LED19 = LEDs [package=led10mm]
  LED22 = LEDs [package=led10mm]
  LED23 = LEDs [package=led10mm]
  LED24 = LEDs [package=led10mm]
  LED26 = LEDs [package=led10mm]
  LED27 = LEDs [package=led10mm]
  LED30 = LEDs [package=led10mm]
  LED31 = LEDs [package=led10mm]
  LED32 = LEDs [package=led10mm]
  R1 = Resistor [tolerance=±5% resistance=430 package=THT]
  R2 = Resistor [tolerance=±5% resistance=430 package=THT]
  R3 = Resistor [tolerance=±5% resistance=430 package=THT]
  R4 = Resistor [tolerance=±5% resistance=430 package=THT]
  R9 = Resistor [tolerance=±5% resistance=430 package=THT]
  R10 = Resistor [tolerance=±5% resistance=430 package=THT]
  R11 = Resistor [tolerance=±5% resistance=430 package=THT]
  R12 = Resistor [tolerance=±5% resistance=430 package=THT]
  R13 = Resistor [tolerance=±5% resistance=430 package=THT]
  R14 = Resistor [tolerance=±5% resistance=430 package=THT]
  R15 = Resistor [tolerance=±5% resistance=430 package=THT]
  R16 = Resistor [tolerance=±5% resistance=430 package=THT]
  R17 = Resistor [tolerance=±5% resistance=430 package=THT]
  R18 = Resistor [tolerance=±5% resistance=430 package=THT]
  R19 = Resistor [tolerance=±5% resistance=430 package=THT]
  R20 = Resistor [tolerance=±5% resistance=430 package=THT]
  R21 = Resistor [tolerance=±5% resistance=430 package=THT]
  R22 = Resistor [tolerance=±5% resistance=430 package=THT]
  R23 = Resistor [tolerance=±5% resistance=430 package=THT]
  R24 = Resistor [tolerance=±5% resistance=430 package=THT]
  J1 = JST-VHR-3N [part_number=JST-VHR-3N package=THT]
  V1 = DC Power [voltage=5]
  U1 = SWITCH-SPST-2 [package=r_sw_th]

nets:
  N1: LED3.C, R1.Pin_0
  N2: LED3.A, LED4.A, LED5.A, LED6.A, LED7.A, LED10.A, LED11.A, LED14.A, LED15.A, LED16.A, LED18.A, LED19.A, LED22.A, LED23.A, LED24.A, LED26.A, LED27.A, LED30.A, LED31.A, LED32.A, J1.pin1, J1.pin_4, U1.P
  N3: LED4.C, R4.Pin_0
  N4: LED5.C, R3.Pin_0
  N5: LED6.C, R2.Pin_0
  N6: LED7.C, R14.Pin_0
  N7: LED10.C, R9.Pin_0
  N8: LED11.C, R10.Pin_0
  N9: LED14.C, R11.Pin_0
  N10: LED15.C, R13.Pin_0
  N11: LED16.C, R12.Pin_0
  N12: LED18.C, R24.Pin_0
  N13: LED19.C, R23.Pin_0
  N14: LED22.C, R16.Pin_0
  N15: LED23.C, R15.Pin_0
  N16: LED24.C, R17.Pin_0
  N17: LED26.C, R19.Pin_0
  N18: LED27.C, R22.Pin_0
  N19: LED30.C, R18.Pin_0
  N20: LED31.C, R20.Pin_0
  N21: LED32.C, R21.Pin_0
  N22: R1.Pin_1, R2.Pin_1, R3.Pin_1, R4.Pin_1, R9.Pin_1, R10.Pin_1, R11.Pin_1, R12.Pin_1, R13.Pin_1, R14.Pin_1, R15.Pin_1, R16.Pin_1, R17.Pin_1, R18.Pin_1, R19.Pin_1, R20.Pin_1, R21.Pin_1, R22.Pin_1, R23.Pin_1, R24.Pin_1, J1.pin_6, V1.V-
  N23: J1.pin2, J1.pin_5, V1.V+, U1.O

// code stored in the sketch: r.ino

